# Fritzing sketch arduino_car (saved by Fritzing 0.9.4)

parts:
  S1 = H-Bridge with L298N
  M1 = DC Motor
  M2 = DC Motor
  Part1 = Arduino Uno (Rev3) - ICSP
  Part2 = Bluetooth HC-05 Macho
  U1 = LIPO-2000mAh [package=lipo-2000]
  hc-sr1 = hc-sr04

nets:
  12V: S1.12V, Part1.VIN, U1.+
  GND: S1.GND, Part1.GND, Part2.GND, U1.-, hc-sr1.GND
  N1: S1.ENA, Part1.D10_PWM/SS
  N2: S1.IN1, Part1.D7
  N3: S1.IN2, Part1.D6_PWM
  N4: S1.IN3, Part1.D5_PWM
  N5: S1.IN4, Part1.D4
  N6: S1.ENB, Part1.D9_PWM
  N7: S1.M1-01, M2.pin_2
  N8: S1.M1-02, M2.pin_1
  N9: S1.M2-01, M1.pin_2
  N10: S1.M2-02, M1.pin_1
  N11: Part1.D11_PWM/MOSI, Part2.TXD
  N12: Part1.D12/MISO, Part2.RXD
  N13: Part1.D2, hc-sr1.Echo
  N14: Part1.D3_PWM, hc-sr1.Trig
  VCC: Part1.5V, Part2.VCC, hc-sr1.VCC

custom parts:
  H-Bridge with L298N: h-bridge

// code stored in the sketch: l298n hc05.ino
#include <SoftwareSerial.h>
#include <TaskScheduler.h>

#define STOP 0
#define FORWARD 1
#define BACKWARD 2
#define TURNLEFT 3
#define TURNRIGHT 4
#define CHANGESPEED 5


#define DEFAULTVOLTAGE 150

#define MINVOLTAGE 0

#define MAXVOLTAGE 255

#define LOWSPEED 0
#define HIGHSPEED 1

SoftwareSerial bluetoothSerial(11, 12); // RX, TX

Scheduler runner;

void ultrasonicTaskCallback();
void bluetoothTaskCallback();

Task bluetoothTask(150,TASK_FOREVER,&bluetoothTaskCallback, &runner, true);
Task ultrasonicTask(500,TASK_FOREVER,&ultrasonicTaskCallback, &runner,true);


// declare motor driver module ctrl pin:
int leftMotorPin1 = 7;
int leftMotorPin2 = 6;
int rightMotorPin1 = 5;
int rightMotorPin2 = 4;

int leftPWM = 10;
int rightPWM = 9;

int ultrasonicInputPin = 3;
int ultrasonicOutputPin = 2;

int motorAction = STOP;
int motorVoltage = MINVOLTAGE;
int motorSpeedLevel = HIGHSPEED;

int distance = 0;
/*
  motor ctrl matrix
  1. stop
  2. forward
  3. backward
  4. turn left
  5. turn right
*/
int ctrlMatrix[5][4] = {
  {LOW, LOW, LOW, LOW},
  {LOW, HIGH, LOW, HIGH},
  {HIGH, LOW, HIGH, LOW},
  {HIGH, LOW, LOW, HIGH},
  {LOW, HIGH, HIGH, LOW}
};


void motorRun(int cmd) {
  Serial.print("recv cmd: ");
  Serial.println(cmd);
  digitalWrite(leftMotorPin1, ctrlMatrix[cmd][0]);
  digitalWrite(leftMotorPin2, ctrlMatrix[cmd][1]);
  digitalWrite(rightMotorPin1, ctrlMatrix[cmd][2]);
  digitalWrite(rightMotorPin2, ctrlMatrix[cmd][3]);
}


void changeSpeed(int voltage) {
  Serial.print("recv voltage: ");
  Serial.println(voltage);
  analogWrite(leftPWM, voltage);
  analogWrite(rightPWM, voltage);
}

void changeSpeedLevel(int level) {
  Serial.print("recv voltage level: ");
  Serial.println(level);
  if (level == HIGHSPEED) {
    analogWrite(leftPWM, MAXVOLTAGE);
    analogWrite(rightPWM, MAXVOLTAGE);
  } else {
    analogWrite(leftPWM, DEFAULTVOLTAGE);
    analogWrite(rightPWM, DEFAULTVOLTAGE);
  }

}
void bluetoothTaskCallback() {
  if (bluetoothSerial.available()) {
    int bluetoothCmd = (int)bluetoothSerial.read();
    Serial.print("bluttooth Command: ");
    Serial.println(bluetoothCmd);
    motorCtrl(bluetoothCmd);
  }
  if (Serial.available()) {
    Serial.print("Serial available: ");
    Serial.println(Serial.read());
    bluetoothSerial.write(Serial.read());
  }
}

void ultrasonicTaskCallback() {
  int distance = getDistance();
  if (distance <= 30) {
    motorRun(STOP);
    Serial.print("distance is dangerous: ");
    Serial.println(distance);
    if (bluetoothSerial.available()) {
      bluetoothSerial.print("distance is dangerous: ");
      bluetoothSerial.println(distance);
    }
    changeSpeedLevel(LOWSPEED);
    motorRun(STOP);
  } else if (distance >= 100) {
    if (bluetoothSerial.available()) {
      bluetoothSerial.print("distance is fine,speed up: ");
      bluetoothSerial.println(distance);
    }
    motorRun(motorAction);
    changeSpeedLevel(HIGHSPEED);
  } else {
    if (bluetoothSerial.available()) {
      bluetoothSerial.print("distance is just ok: ");
      bluetoothSerial.println(distance);
    }
    motorRun(motorAction);
  }

}

void setup()
{
  // put your setup code here, to run once:
  Serial.begin(57600);
  bluetoothSerial.begin(57600);
   bluetoothSerial.print("AT");
  delay(1000);
  bluetoothSerial.println("AT+VERSION");
  delay(1000);
  bluetoothSerial.println("AT+BAUD7");
  delay(1000);
  bluetoothSerial.println("AT+NAMEarduino_car");
  delay(1000);
  // set pin mode for motor
  pinMode(leftMotorPin1, OUTPUT);
  pinMode(leftMotorPin2, OUTPUT);
  pinMode(rightMotorPin1, OUTPUT);
  pinMode(rightMotorPin2, OUTPUT);
  pinMode(leftPWM, OUTPUT);
  pinMode(rightPWM, OUTPUT);

  pinMode(ultrasonicInputPin, INPUT);
  pinMode(ultrasonicOutputPin, OUTPUT);
  changeSpeedLevel(motorSpeedLevel);
  runner.startNow();
  Serial.println("setup has been down.");
}
void motorCtrl(int cmd) {
  if (cmd >= STOP && cmd <= TURNRIGHT) {
    motorAction = cmd;
    motorRun(motorAction);
  } else if (cmd > DEFAULTVOLTAGE && cmd <= MAXVOLTAGE) {
    motorVoltage = cmd;
    changeSpeed(cmd);
  } else if (cmd == CHANGESPEED) {
    if (motorSpeedLevel == LOWSPEED) {
      motorSpeedLevel = HIGHSPEED;
    } else {
      motorSpeedLevel = LOWSPEED;
    }
    changeSpeedLevel(motorSpeedLevel);
  }

}

int getDistance () {
  digitalWrite(ultrasonicOutputPin, LOW);
  delayMicroseconds(2);
  digitalWrite(ultrasonicOutputPin, HIGH);
  delayMicroseconds(10);
  digitalWrite(ultrasonicOutputPin, LOW);

  int distance = pulseIn(ultrasonicInputPin, HIGH);
  distance = distance / 58;
  return distance > 0 ? distance: 0;
}

void loop() {
  runner.execute();
}
